# Fritzing sketch Sketch (saved by Fritzing 0.9.3b)

parts:
  Bauteil1 = Arduino Nano (Rev3.0) (ICSP)
  KY-1 = Keyes Relay [package=THT]

nets:
  N1: Bauteil1.D10, KY-1.signal
  N2: Bauteil1.GND, KY-1.ground
  N3: Bauteil1.5V, KY-1.power

custom parts:
  Keyes Relay: The Keyes 5V relay module is suitable for SCM development, home appliance control. It uses a 5V~12V TIL control signal which can control DC / AC signal.
